# Fritzing sketch FINAL-PROJECT-CAPACITANCE (saved by Fritzing 0.9.3b)
breadboards: 1

parts:
  Part1 = Arduino Uno (Rev3)
  R1 = Resistor [tolerance=±5% resistance=220 package="0805 [SMD]"]
  R2 = Resistor [tolerance=±5% resistance=220 package="0603 [SMD]"]
  C1 = Capacitor Polarized [package=nippon_f80]

nets:
  N1: Part1.A0, R1.Pin_1, R2.Pin_0, C1.-
  N2: Part1.D11_PWM/MOSI, R2.Pin_1
  N3: Part1.D13/SCK, R1.Pin_0
  N4: Part1.GND, C1.+
