# Fritzing sketch FINAL-PROJECT-INDUCTANCE (saved by Fritzing 0.9.3b)
breadboards: 1

parts:
  Part1 = Arduino Uno (Rev3) - ICSP
  U1 = AD8561 - Ultrafast 7ns Single Supply Comparator [part_number=AD8561]
  R1 = Resistor [tolerance=±5% resistance=150 package="1206 [SMD]"]
  D1 = Rectifier Diode [part_number=ln4001 package="Melf DO-213 AA [SMD]"]
  L1 = Inductor [inductance=4µH package="0603 [SMD]"]
  R2 = Resistor [tolerance=±5% resistance=1k package="1206 [SMD]"]
  C1 = Capacitor [package=cap-pth-small2]
  R3 = Resistor [tolerance=±5% resistance=1k package="1206 [SMD]"]

nets:
  N1: Part1.ICSP_MISO, Part1.D12/MISO, R1.Pin_0
  N2: Part1.D3_PWM, U1.V+, R3.Pin_1
  N3: Part1.5V, U1.OUTB, R3.Pin_0
  N4: Part1.GND, U1.V-, L1.pin_1, R2.Pin_0, C1.1
  N5: U1.+IN, R2.Pin_1
  N6: U1.-IN, D1.anode, L1.pin_0, C1.2
  N7: R1.Pin_1, D1.cathode
