# Fritzing sketch MIDTERM-PROJECT (saved by Fritzing 0.9.3b)
breadboards: 1

parts:
  Part1 = Arduino Uno (Rev3)
  R1 = Resistor [tolerance=±5% resistance=150 package="2512 [SMD]"]
  R2 = Resistor [tolerance=±5% resistance=410 package="2512 [SMD]"]
  R3 = Resistor [tolerance=±5% resistance=300 package="2512 [SMD]"]
  R4 = Resistor [tolerance=±5% resistance=500 package="2512 [SMD]"]

nets:
  N1: Part1.A0, R1.Pin_1, R2.Pin_0
  N2: Part1.A1, R2.Pin_1, R3.Pin_0
  N3: Part1.A2, R3.Pin_1, R4.Pin_0
  N4: Part1.5V, R4.Pin_1
  N5: Part1.GND, R1.Pin_0
